// Logisim project cw1lab8.circ as structural Verilog: 1 circuit, main circuit main
module main (
  input  in_1
);

  wire clock_1_out, d_ff_1_q, d_ff_1_qn, nand_1_out, nand_2_out, nand_3_out, nand_4_out, nand_5_out,
       nand_6_out, not_1_out;

  Clock clock_1 (.out(clock_1_out));
  nand nand_1 (nand_1_out, nand_3_out, nand_2_out);
  nand nand_2 (nand_2_out, in_1, nand_4_out);
  not not_1 (not_1_out, clock_1_out);
  nand nand_3 (nand_3_out, nand_1_out, not_1_out);
  nand nand_4 (nand_4_out, nand_3_out, not_1_out, nand_2_out);
  nand nand_5 (nand_5_out, nand_3_out, nand_6_out);
  nand nand_6 (nand_6_out, nand_5_out, nand_4_out);
  D_Flip_Flop #(.trigger("falling")) d_ff_1 (
    .clk(clock_1_out), .D(in_1), .Q(d_ff_1_q), .Qn(d_ff_1_qn));  // open: preset, en, reset
  LED led_1 (.in(nand_5_out));
  LED led_2 (.in(nand_6_out));
  LED led_3 (.in(d_ff_1_q));
  LED led_4 (.in(d_ff_1_qn));
endmodule
