// Logisim project cw1_schemat.circ as structural Verilog: 1 circuit, main circuit main
module main (
);

  wire clock_1_out, j_k_ff_1_q, nand_1_out, nand_2_out, not_1_out, not_2_out, not_3_out, not_4_out,
       shift_register_1_out, shift_register_2_out, xor_1_out, xor_2_out;

  Clock clock_1 (.out(clock_1_out));
  Shift_Register shift_register_1 (
    .clk(clock_1_out), .out(shift_register_1_out));  // open: shift, in, load, clr, d0, q0, d1, q1, d2, q2, d3, q3, d4, q4, d5, q5, d6, q6, d7, q7
  Shift_Register shift_register_2 (
    .clk(clock_1_out), .out(shift_register_2_out));  // open: shift, in, load, clr, d0, q0, d1, q1, d2, q2, d3, q3, d4, q4, d5, q5, d6, q6, d7, q7
  nand nand_1 (nand_1_out, shift_register_1_out, shift_register_2_out);
  not not_1 (not_1_out, shift_register_1_out);
  not not_2 (not_2_out, shift_register_2_out);
  not not_3 (not_3_out, nand_1_out);
  nand nand_2 (nand_2_out, not_1_out, not_2_out);
  not not_4 (not_4_out, nand_2_out);
  J_K_Flip_Flop j_k_ff_1 (
    .J(not_3_out), .clk(clock_1_out), .K(not_4_out), .Q(j_k_ff_1_q));  // open: Qn, preset, en, reset
  xor xor_1 (xor_1_out, shift_register_1_out, shift_register_2_out);
  xor xor_2 (xor_2_out, j_k_ff_1_q, xor_1_out);
  Shift_Register shift_register_3 (
    .in(xor_2_out), .clk(clock_1_out));  // open: shift, out, load, clr, d0, q0, d1, q1, d2, q2, d3, q3, d4, q4, d5, q5, d6, q6, d7, q7

  // Notes on the sheet:
  //   a
  //   b
  //   lub AND-OR-INVERT( ze zwartymi wejściami)
  //   result
endmodule
