// Logisim project cw2_schemat.circ as structural Verilog: 1 circuit, main circuit main
module main (
  input  write,
  input  in_2,
  output out_3,
  output \input ,
  output out_5,
  output out_6,
  output out_7,
  output out_8,
  output out_9,
  output out_10
);

  wire and_1_out, clock_1_out, j_k_ff_1_q, not_1_out, shift_register_1_out, xor_1_out;

  Clock clock_1 (.out(clock_1_out));
  Shift_Register #(.length(4)) shift_register_1 (
    .in(write), .clk(clock_1_out), .out(shift_register_1_out), .q0(out_6), .q1(out_5), .q2(\input ),
    .q3(out_3));  // open: shift, load, clr, d0, d1, d2, d3
  and and_1 (and_1_out, in_2, shift_register_1_out);
  not not_1 (not_1_out, and_1_out);
  J_K_Flip_Flop j_k_ff_1 (
    .J(and_1_out), .clk(clock_1_out), .K(not_1_out), .Q(j_k_ff_1_q));  // open: Qn, preset, en, reset
  xor xor_1 (xor_1_out, j_k_ff_1_q, and_1_out);
  Shift_Register #(.length(4)) shift_register_2 (
    .in(xor_1_out), .clk(clock_1_out), .q0(out_10), .q1(out_9), .q2(out_8), .q3(out_7));  // open: shift, out, load, clr, d0, d1, d2, d3

  // Notes on the sheet:
  //   włączenie układu
  //   output
endmodule
