// Logisim project cw3_schemat.circ as structural Verilog: 1 circuit, main circuit main
module main (
  input  in_1,
  output out_2,
  output out_3
);

  wire clock_1_out, xor_1_out;

  Clock clock_1 (.out(clock_1_out));
  J_K_Flip_Flop j_k_ff_1 (.J(1'b1), .clk(clock_1_out), .K(1'b1), .Q(out_3));  // open: Qn, preset, en, reset
  xor xor_1 (xor_1_out, in_1, out_3);
  J_K_Flip_Flop j_k_ff_2 (.J(xor_1_out), .clk(clock_1_out), .K(xor_1_out), .Q(out_2));  // open: Qn, preset, en, reset
endmodule
