// Logisim project schemat.circ as structural Verilog: 1 circuit, main circuit main
module main (
  input  in_1,
  input  in_2,
  input  in_3,
  input  in_4,
  input  in_5,
  input  in_6,
  input  in_7,
  input  in_8,
  input  in_9,
  input  in_10,
  input  in_11,
  input  in_12,
  input  in_13,
  input  in_14,
  input  in_15,
  input  in_16,
  input  in_17,
  input  in_18,
  input  in_19,
  input  in_20
);

  wire adder_1_cout, adder_1_out, clock_1_out, d_ff_1_q, d_ff_2_q, d_ff_3_q, d_ff_4_q, shift_register_1_out,
       shift_register_2_out;

  Shift_Register shift_register_1 (
    .in(in_19), .clk(clock_1_out), .out(shift_register_1_out), .load(in_10), .d0(in_11), .d1(in_12),
    .d2(in_13), .d3(in_14), .d4(in_15), .d5(in_16), .d6(in_17), .d7(in_18));  // open: shift, clr, q0, q1, q2, q3, q4, q5, q6, q7
  Clock clock_1 (.out(clock_1_out));
  D_Flip_Flop d_ff_1 (.clk(clock_1_out), .D(shift_register_1_out), .Q(d_ff_1_q));  // open: Qn, preset, en, reset
  D_Flip_Flop d_ff_2 (.clk(clock_1_out), .D(d_ff_1_q), .Q(d_ff_2_q));  // open: Qn, preset, en, reset
  D_Flip_Flop d_ff_3 (.clk(clock_1_out), .D(d_ff_2_q), .Q(d_ff_3_q));  // open: Qn, preset, en, reset
  Shift_Register shift_register_2 (
    .in(in_20), .clk(clock_1_out), .out(shift_register_2_out), .load(in_1), .d0(in_2), .d1(in_3), .d2(in_4),
    .d3(in_5), .d4(in_6), .d5(in_7), .d6(in_8), .d7(in_9));  // open: shift, clr, q0, q1, q2, q3, q4, q5, q6, q7
  Adder #(.width(1)) adder_1 (
    .a(shift_register_2_out), .b(d_ff_3_q), .out(adder_1_out), .cin(d_ff_4_q), .cout(adder_1_cout));
  D_Flip_Flop d_ff_4 (.D(adder_1_cout), .Q(d_ff_4_q));  // open: clk, Qn, preset, en, reset
  Shift_Register shift_register_3 (
    .in(adder_1_out), .clk(clock_1_out));  // open: shift, out, load, clr, d0, q0, d1, q1, d2, q2, d3, q3, d4, q4, d5, q5, d6, q6, d7, q7
endmodule
