// Logisim project schemat.circ as structural Verilog: 1 circuit, main circuit main
module main (
);

  wire clock_1_out, not_1_out, shift_register_1_q6;

  Clock clock_1 (.out(clock_1_out));
  Shift_Register shift_register_1 (
    .in(not_1_out), .clk(clock_1_out), .q6(shift_register_1_q6));  // open: shift, out, load, clr, d0, q0, d1, q1, d2, q2, d3, q3, d4, q4, d5, q5, d6, d7, q7
  not not_1 (not_1_out, shift_register_1_q6);
endmodule
